# Fritzing sketch pcb (saved by Fritzing 0.9.3b)
stripboards: 1

parts:
  Part1 = Arduino Nano (Rev3.0) (ICSP)
  J1 = Camdenboss CTB0158-2 [part_number=CTB0158-2 package=THT]
  J2 = Camdenboss CTB0158-2 [part_number=CTB0158-2 package=THT]
  J3 = Camdenboss CTB0158-2 [part_number=CTB0158-2 package=THT]
  LED1 = LED - 5mm [color="Red (633nm)" package="5 mm [THT]"]
  J4 = Piezo Speaker
  LED2 = LED - 5mm [color="Green (555nm)" package="5 mm [THT]"]

nets:
  N1: Part1.GND, J1.pin1, J2.pin2, J3.pin2
  N2: Part1.D2, J1.pin2
  N3: Part1.D8, J2.pin1
  N4: Part1.A1, J3.pin1
  N5: J1.terminal_1, LED1.cathode
  N6: J1.terminal_2, LED1.anode
  N7: J2.terminal_1, LED2.anode
  N8: J2.terminal_2, LED2.cathode
  N9: J3.terminal_1, J4.pin2
  N10: J3.terminal_2, J4.pin1
